# Fritzing sketch LED Signal Testing Circuit (saved by Fritzing 0.9.3b)
breadboards: 3

parts:
  Part1 = Arduino Uno (Rev3)
  R1 = Resistor [tolerance=±5% resistance=220 package=THT]
  Left = smd LED [color="Red (633nm)" package="1206 [SMD]"]
  Right = smd LED [color="Red (633nm)" package="1206 [SMD]"]
  Brake = smd LED [color="Red (633nm)" package="1206 [SMD]"]
  R2 = Resistor [tolerance=±5% resistance=220 package=THT]
  R3 = Resistor [tolerance=±5% resistance=220 package=THT]
  D1 = Rectifier Diode [part_number=1N4001 package="300 mil [THT]"]
  D2 = Rectifier Diode [part_number=1N4001 package="300 mil [THT]"]
  D3 = Rectifier Diode [part_number=1N4001 package="300 mil [THT]"]
  D4 = Rectifier Diode [part_number=1N4001 package="300 mil [THT]"]
  Right_Button = Pushbutton [package="[SMD]"]
  4_Wire_Brake_Button = Pushbutton [package="[SMD]"]
  5_Wire_Brake_Button = Pushbutton [package="[SMD]"]
  Emergency_Flahsers_Button = Pushbutton [package="[SMD]"]
  Left_Button = Pushbutton [package="[SMD]"]
  R5 = Resistor [tolerance=±5% resistance=220 package=THT]
  R7 = Resistor [tolerance=±5% resistance=220 package=THT]
  R8 = Resistor [tolerance=±5% resistance=220 package=THT]
  R9 = Resistor [tolerance=±5% resistance=220 package=THT]
  R10 = Resistor [tolerance=±5% resistance=220 package=THT]
  D5 = Rectifier Diode [part_number=1N4001 package="300 mil [THT]"]
  D6 = Rectifier Diode [part_number=1N4001 package="300 mil [THT]"]

nets:
  N1: Part1.D8, D6.anode
  N2: Part1.D9_PWM, D1.anode, D2.anode
  N3: Part1.D10_PWM/SS, R3.Pin_0
  N4: Part1.D11_PWM/MOSI, D3.anode, D4.anode
  N5: Part1.D2, Left_Button.Pin_1
  N6: Part1.D3_PWM, Right_Button.Pin_1, Right_Button.Pin_2
  N7: Part1.D4, 4_Wire_Brake_Button.Pin_1, 4_Wire_Brake_Button.Pin_2
  N8: Part1.D5_PWM, 5_Wire_Brake_Button.Pin_1, 5_Wire_Brake_Button.Pin_2
  N9: Part1.D6_PWM, Emergency_Flahsers_Button.Pin_1, Emergency_Flahsers_Button.Pin_2
  N10: Part1.D7, D5.anode
  N11: Part1.GND, Left.cathode, Right.cathode, Brake.cathode, R5.Pin_1, R7.Pin_1, R8.Pin_1, R9.Pin_1, R10.Pin_1
  N12: R1.Pin_0, D1.cathode, D3.cathode, D5.cathode
  N13: R1.Pin_1, Left.anode
  N14: Right.anode, R2.Pin_1
  N15: Brake.anode, R3.Pin_1
  N16: R2.Pin_0, D2.cathode, D4.cathode, D6.cathode
